# Fritzing sketch schematic-fritzing (saved by Fritzing 0.9.2b)
breadboards: 7

parts:
  M1 = DC Motor
  M2 = DC Motor
  Componente2 = SRF05 Ultrasonic Rangefinder
  Componente3 = SRF05 Ultrasonic Rangefinder
  Componente4 = SRF05 Ultrasonic Rangefinder
  IC1 = L293D [package=THT]
  VCC1 = 9V Battery
  Componente1 = Arduino Uno (Rev3)

nets:
  N1: M1.pin_1, IC1.Out_2_(_Controlled_by_Enable_1_)
  N2: M1.pin_2, IC1.Out_1_(_Controlled_by_Enable_1_)
  N3: M2.pin_1, IC1.Out_4_(_Controlled_by_Enable_2_)
  N4: M2.pin_2, IC1.Out_3_(_Controlled_by_Enable_2_)
  VCC: Componente2.VCC, Componente3.VCC, Componente4.VCC, IC1.+V, Componente1.5V
  N5: Componente2.Trig, Componente1.A2
  N6: Componente2.Echo, Componente1.A3
  GND: Componente2.GND, Componente3.GND, Componente4.GND, IC1.0V, VCC1.-, Componente1.GND
  N7: Componente3.Trig, Componente1.A4/SDA
  N8: Componente3.Echo, Componente1.A5/SCL
  N9: Componente4.Trig, Componente1.A0
  N10: Componente4.Echo, Componente1.A1
  N11: IC1.Enable_1, Componente1.D10_PWM/SS
  N12: IC1.In_1, Componente1.D9_PWM
  N13: IC1.In_2, Componente1.D8
  N14: IC1.+Vmotor, VCC1.+, Componente1.VIN
  N15: IC1.Enable_2, Componente1.D11_PWM/MOSI
  N16: IC1.In_3, Componente1.D7
  N17: IC1.In_4, Componente1.D12/MISO

custom parts:
  9V Battery: Your standard 9V battery
